# Fritzing sketch BRAWLER_Rev7_LightSensing (saved by Fritzing 0.9.1b)
breadboards: 1

parts:
  Part1 = Arduino Uno (Rev3)
  R1 = Photocell (LDR) [package=THT]
  S2 = Pushbutton [package="[THT]"]
  S3 = Pushbutton [package="[THT]"]
  R2 = Resistor [tolerance=±5% resistance=10k package=THT]
  R3 = Resistor [tolerance=±5% resistance=10k package=THT]
  R4 = Resistor [tolerance=±5% resistance=10k package=THT]
  Power_plug1 = Power plug
  J1 = Basic Servo

nets:
  N1: Part1.A0, R1.pin_0, R4.Pin_0
  N2: Part1.D9_PWM, J1.pulse
  GND: Part1.GND, R2.Pin_1, R3.Pin_1, R4.Pin_1, Power_plug1.GND, J1.gnd
  N3: Part1.D2, S3.Pin_1, S3.Pin_2, R3.Pin_0
  N4: Part1.D3_PWM, S2.Pin_1, S2.Pin_2, R2.Pin_0
  VCC: Part1.5V, R1.pin_1, S2.Pin_3, S2.Pin_4, S3.Pin_3, S3.Pin_4, Power_plug1.VCC, J1.vcc

// code stored in the sketch: BRAB_Rev1fzz.ino
#include <Servo.h>

//pin configuration
int servoPin = 9;
int photocellPin = A0; //in analog pin 
const int button1_pin = 2;
const int button2_pin = 3;
const int killswitch = 4;

//interger varibles for program

Servo myservo;  // create servo object t control 
int photocellReading; // the analog reading from light depended resistor
int button1_value;  //high or low button values
int button2_value; //high or low button value
int killswitch_value;  //high or low killswitch values
int state = 0; //keeps state to not over spin 
int prevstate = 0; //Keeps history of prior state
int sensorValue = 0;  // stores LDR value
int dirc = 0;   // continuous servo direction 
int time = 0;  //time to spin that direction

//main loop
void setup(void) 
{
  Serial.begin(9600);   //Debug via Serial
  myservo.attach(servoPin);   // Attach servo to servoPin
  pinMode(button1_pin, INPUT);  //sets button 1 pin as input
  pinMode(button2_pin, INPUT);  //sets button 2 pin as input
  pinMode(killswitch, INPUT);   //sets kill swtich as input
}


void loop(void) {
  Serial.println("Start of main loop, pootie");
  killswitch_value = digitalRead(killswitch); //reads value of killswtich
  button1_value = digitalRead(button1_pin);  //reads value of button1_pin
  button2_value = digitalRead(button2_pin);  //reads value of button2_pin
  state=1; // start with blinds closed
  if(killswitch_value==HIGH) { //IF Killswtich isn't set then run main loop
    photocellReading = analogRead(photocellPin); //Query LDR
    Serial.print("Light Reading :");  
    Serial.print(photocellReading); // Prints raw analog reading from LDR
    Serial.print(" | State: ");
    Serial.print(state); // prints the the current state

    //Define modes based on bightness and set corresponding servo direction and time
    if (photocellReading < 500) {
      Serial.println("Night");
      dirc=180; // direction for servo to run
      time=150; //time for servo to run in 
      state=1; //sets state
    } 
    else if (photocellReading > 500) {
      Serial.println("Very day, much sun");
      dirc=0; // direction for servo to run
      time=150; //time for servo to run in 
      state=2; //sets state
    }
    else if (button1_value==LOW) {
    Serial.println("button 1 pushed");
      dirc=180; // direction for servo to run
      time=150; //time for servo to run in 
      state=1; //sets state
      }
    else if (button2_value==LOW) {
      Serial.println("button 2 pushed");
      dirc=0; // direction for servo to run
      time=150; //time for servo to run in 
      state=2; //sets state
  }
  else {
    Serial.println("Nothing low, kill switch HIGH");
    return;
  }
  } 
  if (state != prevstate){ //IF the photocell reading is different from last sample then execute servo controls
    ldr_press();
  }
  else{
    Serial.println("end of main loop, dawg. Same state");
  }
}

void ldr_press() { //executes after photocell reads
  Serial.println("State Change. Rotating Servo");
  myservo.attach(servoPin);
  myservo.write(dirc);
  delay(time);
  myservo.detach();
  return;
}
